# Fritzing sketch autoprint_schematic (saved by Fritzing 0.9.4)

parts:
  Raspberry_Pi_1 = Raspberry Pi 3 [part_number=RPI-3-V1.2]
  KY-1 = Keyes Relay [package=THT]
  KY-2 = Keyes Relay [package=THT]
  J1 = Camdenboss CTB0158-3 [part_number=CTB0158-3 package=THT]
  J2 = Camdenboss CTB0158-3 [part_number=CTB0158-3 package=THT]
  J3 = Camdenboss CTB0158-3 [part_number=CTB0158-3 package=THT]

nets:
  N1: Raspberry_Pi_1.GND, KY-1.power, KY-2.power
  N2: Raspberry_Pi_1.GIPO24, KY-2.ground
  N3: Raspberry_Pi_1.GIPO23, KY-1.ground
  N4: Raspberry_Pi_1.5V, KY-1.signal, KY-2.signal
  N5: KY-1.NC, KY-1.C, KY-2.NC, KY-2.C, KY-2.NO, J1.terminal_3, J3.terminal_1
  N6: KY-1.NO, J2.terminal_1
  N7: J1.terminal_1, J2.terminal_3, J3.terminal_3
  N8: J1.terminal_2, J2.terminal_2, J3.terminal_2

notes:
  Mains IN
  Printer OUT
  Light OUT

custom parts:
  Keyes Relay: The Keyes 5V relay module is suitable for SCM development, home appliance control. It uses a 5V~12V TIL control signal which can control DC / AC signal.
